# Fritzing sketch selfieHouseConexion (saved by Fritzing 0.9.3b)
breadboards: 1

parts:
  U1 = NodeMCU V1.0  # not connected
  RHT1 = Humidity and Temperature Sensor RHT03
  J1 = Piezo Speaker
  LED1 = LED - 5mm [color="Yellow (592nm)" package="5 mm [THT]"]
  LED2 = LED - 5mm [color="Blue (505nm)" package="5 mm [THT]"]
  PIR1 = PIR sensor
  F1 = Fan - Ventilador [package=THT]
  Grove1 = Grove Light Sensor
  S1 = KY-026
  R1 = Resistor [tolerance=±5% resistance=10k package="0805 [SMD]"]
  R2 = Resistor [tolerance=±5% resistance=1k package="0805 [SMD]"]
  R3 = Resistor [tolerance=±5% resistance=1k package="0805 [SMD]"]
  J2 = Basic Servo

nets:
  VCC: RHT1.Vcc, PIR1.VDD, Grove1.VCC, S1.pin3, R1.Pin_1, J2.vcc
  N1: RHT1.Data-signal, R1.Pin_0
  GND: RHT1.GND_2, PIR1.GND, Grove1.GND, S1.pin2, J2.gnd
  N2: J1.pin1, LED1.cathode, LED2.cathode, F1.GND
  N3: LED1.anode, R3.Pin_0
  N4: LED2.anode, R2.Pin_0

notes:
  Linea de 3,3v
  Linea de 5v
  Hay que probar con este sensor y ver si es necesario
  CABLE ROJO: VCC +
  CABLE NEGRO: GND
  CABLE COLOR: DATOS

custom parts:
  NodeMCU V1.0: ESP8266 based NodeMCU
  Fan - Ventilador: Ventilador de 2 pines, se encuentra comunmente en computadoras de escritorio
  KY-026: ky-026 flame sensor module
